// Logisim project 8-bit computerv2.circ as structural Verilog: 3 circuits, main circuit main
module main (
  input  Memory_In,
  input  [7:0] Memory_Address,
  input  [11:0] Memory_Data
);

  wire A_IN, A_OUT, adder_1_cout, ALU_OUT, and_1_out, and_2_out, and_3_out, and_4_out, B_IN, B_OUT,
       buffer_1_out, buffer_2_out, buffer_3_out, C_IN, C_OUT, Clear_Memory_out, Clock_out,
       controlled_buffer_30_out, controlled_buffer_31_out, COUNTER_INCREMENT, COUNTER_OUT, decoder_1_out0,
       decoder_1_out1, decoder_1_out2, decoder_1_out3, decoder_2_out0, decoder_2_out1, decoder_2_out2,
       decoder_2_out3, decoder_2_out4, decoder_2_out5, decoder_2_out6, decoder_2_out7, decoder_2_out8,
       decoder_2_out9, decoder_2_out10, decoder_2_out11, decoder_2_out12, decoder_2_out13, decoder_2_out14,
       decoder_2_out15, F_IN, Flag_Register_q, HALT, IR_IN, IR_OUT, JUMP, logic_1_mar_a_in, logic_1_mar_b_in,
       logic_1_ram_a_out, logic_1_ram_b_out, Manual_Clock_2, MAR_A_IN, nor_1_out, nor_2_out, nor_3_out,
       nor_4_out, not_1_out, not_2_out, not_3_out, not_4_out, or_1_out, or_2_out, or_5_out, or_6_out,
       OUT_ENABLE, overflow_1_overflow, RAM_A_IN, RAM_A_OUT, Reset_Computer_out, reset_MARA, reset_Out,
       reset_PC, reset_RAMA, reset_RegA, reset_RegB, reset_RegC, reset_RegF, reset_RegI, reset_SC,
       Save_value_out, SUB;
  wire [1:0] Step_Counter_q;
  wire [3:0] Instruction_Register_q_2;
  wire [7:0] adder_1_out, buffer_4_out, controlled_buffer_1_out, controlled_buffer_5_out,
       Instruction_Register_q, Memory_Address_Register_A_q, Output_Register_q, Program_Counter_q,
       Register_A_q, Register_B_q, Register_C_q, xor_1_out;
  wire [11:0] controlled_buffer_2_out, ram_1_data;

  and and_1 (and_1_out, 1'b1, not_1_out);
  not not_1 (not_1_out, Memory_In);
  buf buffer_1 (buffer_1_out, RAM_A_IN);
  assign controlled_buffer_1_out = Memory_In ? Memory_Address : 8'bz;  // Controlled_Buffer controlled_buffer_1
  assign controlled_buffer_2_out = Memory_In ? Memory_Data : 12'bz;  // Controlled_Buffer controlled_buffer_2
  or or_1 (or_1_out, buffer_1_out, buffer_2_out);
  not not_2 (not_2_out, Memory_In);
  Counter #(.ongoal("stay")) Program_Counter (
    .load(JUMP), .D(controlled_buffer_5_out), .count(COUNTER_INCREMENT), .Q(Program_Counter_q),
    .clk(controlled_buffer_31_out), .clr(reset_PC));  // open: carry
  Register Memory_Address_Register_A (
    .D(controlled_buffer_5_out), .en(MAR_A_IN), .Q(Memory_Address_Register_A_q),
    .clk(controlled_buffer_31_out), .clr(reset_MARA));
  assign controlled_buffer_1_out = and_1_out ? Memory_Address_Register_A_q : 8'bz;  // Controlled_Buffer controlled_buffer_3
  buf buffer_2 (buffer_2_out, Memory_In);
  Register #(.width(12)) Instruction_Register (
    .D(ram_1_data), .en(IR_IN), .Q({Instruction_Register_q_2, Instruction_Register_q}),
    .clk(controlled_buffer_31_out), .clr(reset_RegI));
  RAM #(.dataWidth(12), .bus("separate")) ram_1 (
    .addr(controlled_buffer_1_out), .din(controlled_buffer_2_out), .data(ram_1_data), .str(or_1_out),
    .sel(1'b1), .clk(buffer_3_out), .ld(1'b1), .clr(reset_RAMA));
  assign controlled_buffer_2_out = not_2_out ? {4'b0000, buffer_4_out} : 12'bz;  // Controlled_Buffer controlled_buffer_4
  assign controlled_buffer_5_out[0] = COUNTER_OUT ? Program_Counter_q[0] : 1'bz;  // Controlled_Buffer controlled_buffer_5
  assign controlled_buffer_5_out[1] = COUNTER_OUT ? Program_Counter_q[1] : 1'bz;  // Controlled_Buffer controlled_buffer_6
  assign controlled_buffer_5_out[2] = COUNTER_OUT ? Program_Counter_q[2] : 1'bz;  // Controlled_Buffer controlled_buffer_7
  assign controlled_buffer_5_out[3] = COUNTER_OUT ? Program_Counter_q[3] : 1'bz;  // Controlled_Buffer controlled_buffer_8
  assign controlled_buffer_5_out[4] = COUNTER_OUT ? Program_Counter_q[4] : 1'bz;  // Controlled_Buffer controlled_buffer_9
  assign controlled_buffer_5_out[5] = COUNTER_OUT ? Program_Counter_q[5] : 1'bz;  // Controlled_Buffer controlled_buffer_10
  assign controlled_buffer_5_out[6] = COUNTER_OUT ? Program_Counter_q[6] : 1'bz;  // Controlled_Buffer controlled_buffer_11
  assign controlled_buffer_5_out[7] = COUNTER_OUT ? Program_Counter_q[7] : 1'bz;  // Controlled_Buffer controlled_buffer_12
  buf buffer_3 (buffer_3_out, controlled_buffer_31_out);
  assign buffer_3_out = Memory_In ? Manual_Clock_2 : 1'bz;  // Controlled_Buffer controlled_buffer_13
  assign controlled_buffer_5_out[0] = RAM_A_OUT ? ram_1_data[0] : 1'bz;  // Controlled_Buffer controlled_buffer_14
  assign controlled_buffer_5_out[1] = RAM_A_OUT ? ram_1_data[1] : 1'bz;  // Controlled_Buffer controlled_buffer_15
  assign controlled_buffer_5_out[2] = RAM_A_OUT ? ram_1_data[2] : 1'bz;  // Controlled_Buffer controlled_buffer_16
  assign controlled_buffer_5_out[3] = RAM_A_OUT ? ram_1_data[3] : 1'bz;  // Controlled_Buffer controlled_buffer_17
  assign controlled_buffer_5_out[4] = RAM_A_OUT ? ram_1_data[4] : 1'bz;  // Controlled_Buffer controlled_buffer_18
  assign controlled_buffer_5_out[5] = RAM_A_OUT ? ram_1_data[5] : 1'bz;  // Controlled_Buffer controlled_buffer_19
  assign controlled_buffer_5_out[6] = RAM_A_OUT ? ram_1_data[6] : 1'bz;  // Controlled_Buffer controlled_buffer_20
  assign controlled_buffer_5_out[7] = RAM_A_OUT ? ram_1_data[7] : 1'bz;  // Controlled_Buffer controlled_buffer_21
  buf buffer_4 (buffer_4_out[0], controlled_buffer_5_out[0]);
  buf buffer_5 (buffer_4_out[1], controlled_buffer_5_out[1]);
  buf buffer_6 (buffer_4_out[2], controlled_buffer_5_out[2]);
  buf buffer_7 (buffer_4_out[3], controlled_buffer_5_out[3]);
  buf buffer_8 (buffer_4_out[4], controlled_buffer_5_out[4]);
  buf buffer_9 (buffer_4_out[5], controlled_buffer_5_out[5]);
  buf buffer_10 (buffer_4_out[6], controlled_buffer_5_out[6]);
  buf buffer_11 (buffer_4_out[7], controlled_buffer_5_out[7]);
  assign controlled_buffer_5_out[0] = IR_OUT ? Instruction_Register_q[0] : 1'bz;  // Controlled_Buffer controlled_buffer_22
  assign controlled_buffer_5_out[1] = IR_OUT ? Instruction_Register_q[1] : 1'bz;  // Controlled_Buffer controlled_buffer_23
  assign controlled_buffer_5_out[2] = IR_OUT ? Instruction_Register_q[2] : 1'bz;  // Controlled_Buffer controlled_buffer_24
  assign controlled_buffer_5_out[3] = IR_OUT ? Instruction_Register_q[3] : 1'bz;  // Controlled_Buffer controlled_buffer_25
  assign controlled_buffer_5_out[4] = IR_OUT ? Instruction_Register_q[4] : 1'bz;  // Controlled_Buffer controlled_buffer_26
  assign controlled_buffer_5_out[5] = IR_OUT ? Instruction_Register_q[5] : 1'bz;  // Controlled_Buffer controlled_buffer_27
  assign controlled_buffer_5_out[6] = IR_OUT ? Instruction_Register_q[6] : 1'bz;  // Controlled_Buffer controlled_buffer_28
  assign controlled_buffer_5_out[7] = IR_OUT ? Instruction_Register_q[7] : 1'bz;  // Controlled_Buffer controlled_buffer_29
  Clock Clock (.out(Clock_out));
  not not_3 (not_3_out, HALT);
  assign controlled_buffer_30_out = not_3_out ? Clock_out : 1'bz;  // Controlled_Buffer controlled_buffer_30
  not not_4 (not_4_out, Memory_In);
  assign controlled_buffer_31_out = not_4_out ? controlled_buffer_30_out : 1'bz;  // Controlled_Buffer controlled_buffer_31
  assign controlled_buffer_5_out[0] = A_OUT ? Register_A_q[0] : 1'bz;  // Controlled_Buffer controlled_buffer_32
  assign controlled_buffer_5_out[1] = A_OUT ? Register_A_q[1] : 1'bz;  // Controlled_Buffer controlled_buffer_33
  assign controlled_buffer_5_out[2] = A_OUT ? Register_A_q[2] : 1'bz;  // Controlled_Buffer controlled_buffer_34
  assign controlled_buffer_5_out[3] = A_OUT ? Register_A_q[3] : 1'bz;  // Controlled_Buffer controlled_buffer_35
  assign controlled_buffer_5_out[4] = A_OUT ? Register_A_q[4] : 1'bz;  // Controlled_Buffer controlled_buffer_36
  assign controlled_buffer_5_out[5] = A_OUT ? Register_A_q[5] : 1'bz;  // Controlled_Buffer controlled_buffer_37
  assign controlled_buffer_5_out[6] = A_OUT ? Register_A_q[6] : 1'bz;  // Controlled_Buffer controlled_buffer_38
  assign controlled_buffer_5_out[7] = A_OUT ? Register_A_q[7] : 1'bz;  // Controlled_Buffer controlled_buffer_39
  assign controlled_buffer_5_out[0] = B_OUT ? Register_B_q[0] : 1'bz;  // Controlled_Buffer controlled_buffer_40
  assign controlled_buffer_5_out[1] = B_OUT ? Register_B_q[1] : 1'bz;  // Controlled_Buffer controlled_buffer_41
  assign controlled_buffer_5_out[2] = B_OUT ? Register_B_q[2] : 1'bz;  // Controlled_Buffer controlled_buffer_42
  assign controlled_buffer_5_out[3] = B_OUT ? Register_B_q[3] : 1'bz;  // Controlled_Buffer controlled_buffer_43
  assign controlled_buffer_5_out[4] = B_OUT ? Register_B_q[4] : 1'bz;  // Controlled_Buffer controlled_buffer_44
  assign controlled_buffer_5_out[5] = B_OUT ? Register_B_q[5] : 1'bz;  // Controlled_Buffer controlled_buffer_45
  assign controlled_buffer_5_out[6] = B_OUT ? Register_B_q[6] : 1'bz;  // Controlled_Buffer controlled_buffer_46
  assign controlled_buffer_5_out[7] = B_OUT ? Register_B_q[7] : 1'bz;  // Controlled_Buffer controlled_buffer_47
  assign controlled_buffer_5_out[0] = ALU_OUT ? adder_1_out[0] : 1'bz;  // Controlled_Buffer controlled_buffer_48
  assign controlled_buffer_5_out[1] = ALU_OUT ? adder_1_out[1] : 1'bz;  // Controlled_Buffer controlled_buffer_49
  assign controlled_buffer_5_out[2] = ALU_OUT ? adder_1_out[2] : 1'bz;  // Controlled_Buffer controlled_buffer_50
  assign controlled_buffer_5_out[3] = ALU_OUT ? adder_1_out[3] : 1'bz;  // Controlled_Buffer controlled_buffer_51
  assign controlled_buffer_5_out[4] = ALU_OUT ? adder_1_out[4] : 1'bz;  // Controlled_Buffer controlled_buffer_52
  assign controlled_buffer_5_out[5] = ALU_OUT ? adder_1_out[5] : 1'bz;  // Controlled_Buffer controlled_buffer_53
  assign controlled_buffer_5_out[6] = ALU_OUT ? adder_1_out[6] : 1'bz;  // Controlled_Buffer controlled_buffer_54
  assign controlled_buffer_5_out[7] = ALU_OUT ? adder_1_out[7] : 1'bz;  // Controlled_Buffer controlled_buffer_55
  assign controlled_buffer_5_out[0] = C_OUT ? Register_C_q[0] : 1'bz;  // Controlled_Buffer controlled_buffer_56
  assign controlled_buffer_5_out[1] = C_OUT ? Register_C_q[1] : 1'bz;  // Controlled_Buffer controlled_buffer_57
  assign controlled_buffer_5_out[2] = C_OUT ? Register_C_q[2] : 1'bz;  // Controlled_Buffer controlled_buffer_58
  assign controlled_buffer_5_out[3] = C_OUT ? Register_C_q[3] : 1'bz;  // Controlled_Buffer controlled_buffer_59
  assign controlled_buffer_5_out[4] = C_OUT ? Register_C_q[4] : 1'bz;  // Controlled_Buffer controlled_buffer_60
  assign controlled_buffer_5_out[5] = C_OUT ? Register_C_q[5] : 1'bz;  // Controlled_Buffer controlled_buffer_61
  assign controlled_buffer_5_out[6] = C_OUT ? Register_C_q[6] : 1'bz;  // Controlled_Buffer controlled_buffer_62
  assign controlled_buffer_5_out[7] = C_OUT ? Register_C_q[7] : 1'bz;  // Controlled_Buffer controlled_buffer_63
  LED led_1 (.in(Register_A_q[4]));
  LED led_2 (.in(Register_A_q[5]));
  LED led_3 (.in(Register_A_q[6]));
  LED led_4 (.in(Register_A_q[7]));
  LED led_5 (.in(Register_B_q[6]));
  LED led_6 (.in(Register_B_q[4]));
  LED led_7 (.in(Register_B_q[5]));
  LED led_8 (.in(Register_B_q[7]));
  LED led_9 (.in(adder_1_out[6]));
  LED led_10 (.in(adder_1_out[4]));
  LED led_11 (.in(adder_1_out[7]));
  LED led_12 (.in(adder_1_out[5]));
  LED led_13 (.in(Register_C_q[7]));
  LED led_14 (.in(Register_C_q[6]));
  LED led_15 (.in(Register_C_q[4]));
  LED led_16 (.in(Register_C_q[5]));
  LED led_17 (.in(Register_A_q[1]));
  LED led_18 (.in(Register_A_q[2]));
  LED led_19 (.in(Register_A_q[3]));
  LED led_20 (.in(Register_A_q[0]));
  LED led_21 (.in(Register_B_q[0]));
  LED led_22 (.in(Register_B_q[1]));
  LED led_23 (.in(Register_B_q[2]));
  LED led_24 (.in(Register_B_q[3]));
  LED led_25 (.in(adder_1_out[0]));
  LED led_26 (.in(adder_1_out[2]));
  LED led_27 (.in(adder_1_out[3]));
  LED led_28 (.in(adder_1_out[1]));
  LED led_29 (.in(Register_C_q[0]));
  LED led_30 (.in(Register_C_q[3]));
  LED led_31 (.in(Register_C_q[2]));
  LED led_32 (.in(Register_C_q[1]));
  Register Output_Register (
    .D(controlled_buffer_5_out), .en(OUT_ENABLE), .Q(Output_Register_q), .clk(controlled_buffer_31_out),
    .clr(reset_Out));
  Counter #(.width(2), .max('h3)) Step_Counter (
    .count(1'b1), .Q(Step_Counter_q), .clk(controlled_buffer_31_out), .clr(reset_SC));  // open: load, D, carry
  Register Register_A (
    .D(controlled_buffer_5_out), .en(A_IN), .Q(Register_A_q), .clk(controlled_buffer_31_out), .clr(reset_RegA));
  Register Register_B (
    .D(controlled_buffer_5_out), .en(B_IN), .Q(Register_B_q), .clk(controlled_buffer_31_out), .clr(reset_RegB));
  Register Register_C (
    .D(controlled_buffer_5_out), .en(C_IN), .Q(Register_C_q), .clk(controlled_buffer_31_out), .clr(reset_RegC));
  Decoder #(.select(2)) decoder_1 (
    .out0(decoder_1_out0), .out1(decoder_1_out1), .out2(decoder_1_out2), .out3(decoder_1_out3),
    .sel(Step_Counter_q), .en(1'b1));
  Decoder #(.select(4)) decoder_2 (
    .out0(decoder_2_out0), .out1(decoder_2_out1), .out2(decoder_2_out2), .out3(decoder_2_out3),
    .out4(decoder_2_out4), .out5(decoder_2_out5), .out6(decoder_2_out6), .out7(decoder_2_out7),
    .out8(decoder_2_out8), .out9(decoder_2_out9), .out10(decoder_2_out10), .out11(decoder_2_out11),
    .out12(decoder_2_out12), .out13(decoder_2_out13), .out14(decoder_2_out14), .out15(decoder_2_out15),
    .sel(Instruction_Register_q_2), .en(1'b1));
  xor xor_1 (xor_1_out[0], Register_B_q[0], SUB);
  xor xor_2 (xor_1_out[1], Register_B_q[1], SUB);
  xor xor_3 (xor_1_out[2], Register_B_q[2], SUB);
  xor xor_4 (xor_1_out[3], Register_B_q[3], SUB);
  xor xor_5 (xor_1_out[4], Register_B_q[4], SUB);
  xor xor_6 (xor_1_out[5], Register_B_q[5], SUB);
  xor xor_7 (xor_1_out[6], Register_B_q[6], SUB);
  xor xor_8 (xor_1_out[7], Register_B_q[7], SUB);
  LED led_33 (.in(Output_Register_q[6]));
  LED led_34 (.in(Output_Register_q[4]));
  LED led_35 (.in(Output_Register_q[5]));
  LED led_36 (.in(Output_Register_q[7]));
  nor nor_1 (nor_1_out, Register_C_q[0], Register_C_q[1]);
  nor nor_2 (nor_2_out, Register_C_q[2], Register_C_q[3]);
  nor nor_3 (nor_3_out, Register_C_q[4], Register_C_q[5]);
  nor nor_4 (nor_4_out, Register_C_q[6], Register_C_q[7]);
  LED led_37 (.in(Output_Register_q[1]));
  LED led_38 (.in(Output_Register_q[2]));
  LED led_39 (.in(Output_Register_q[3]));
  LED led_40 (.in(Output_Register_q[0]));
  Adder adder_1 (.a(Register_A_q), .b(xor_1_out), .out(adder_1_out), .cin(SUB), .cout(adder_1_cout));
  and and_2 (and_2_out, nor_1_out, nor_2_out);
  and and_3 (and_3_out, and_2_out, and_4_out);
  and and_4 (and_4_out, nor_3_out, nor_4_out);
  overflow overflow_1 (
    .Value_A(Register_A_q), .Value_B(Register_B_q), .Output_Value(adder_1_out), .SUB(SUB),
    .Overflow(overflow_1_overflow));
  LED _0_Flag (.in(and_3_out));
  \logic  logic_1 (
    .sc0(decoder_1_out0), .sc1(decoder_1_out1), .sc2(decoder_1_out2), .Bit_1(Instruction_Register_q[0]),
    .Bit_2(Instruction_Register_q[1]), .Bit_5(Instruction_Register_q[4]), .Bit_6(Instruction_Register_q[5]),
    .Flag_Register_Bit(Flag_Register_q), ._0_Flag(and_3_out), ._0000(decoder_2_out0), ._0001(decoder_2_out1),
    ._0010(decoder_2_out2), ._0011(decoder_2_out3), ._0100(decoder_2_out4), ._0101(decoder_2_out5),
    ._0110(decoder_2_out6), ._0111(decoder_2_out7), ._1000(decoder_2_out8), ._1001(decoder_2_out9),
    ._1010(decoder_2_out10), ._1011(decoder_2_out11), ._1100(decoder_2_out12), ._1101(decoder_2_out13),
    ._1110(decoder_2_out14), ._1111(decoder_2_out15), .sc3(decoder_1_out3), .COUNTER_OUT(COUNTER_OUT),
    .RAM_B_OUT(logic_1_ram_b_out), .MAR_B_IN(logic_1_mar_b_in), .IR_IN(IR_IN),
    .COUNTER_INCREMENT(COUNTER_INCREMENT), .A_IN(A_IN), .A_OUT(A_OUT), .B_IN(B_IN), .B_OUT(B_OUT),
    .C_IN(C_IN), .C_OUT(C_OUT), .OUT_ENABLE(OUT_ENABLE), .ALU_OUT(ALU_OUT), .SUB(SUB), .JUMP(JUMP),
    .RAM_A_IN(RAM_A_IN), .RAM_A_OUT(logic_1_ram_a_out), .MAR_A_IN(logic_1_mar_a_in), .HALT(HALT),
    .F_IN(F_IN), .IR_OUT(IR_OUT));
  or or_2 (or_2_out, adder_1_cout, overflow_1_overflow);
  Register #(.width(1)) Flag_Register (
    .D(or_2_out), .en(F_IN), .Q(Flag_Register_q), .clk(controlled_buffer_31_out), .clr(reset_RegF));
  LED Carry_Overflow_Flag (.in(Flag_Register_q));
  or or_3 (RAM_A_OUT, logic_1_ram_a_out, logic_1_ram_b_out);
  or or_4 (MAR_A_IN, logic_1_mar_a_in, logic_1_mar_b_in);
  buf buffer_12 (reset_RegA, Reset_Computer_out);
  buf buffer_13 (reset_RegB, Reset_Computer_out);
  buf buffer_14 (reset_RegC, Reset_Computer_out);
  buf buffer_15 (reset_Out, Reset_Computer_out);
  buf buffer_16 (reset_RegF, Reset_Computer_out);
  buf buffer_17 (reset_SC, Reset_Computer_out);
  buf buffer_18 (reset_RegI, Reset_Computer_out);
  buf buffer_19 (reset_MARA, Reset_Computer_out);
  buf buffer_20 (reset_PC, Reset_Computer_out);
  buf buffer_21 (reset_RAMA, Clear_Memory_out);
  LED led_41 (.in(A_IN));
  LED led_42 (.in(A_OUT));
  LED led_43 (.in(B_IN));
  LED led_44 (.in(B_OUT));
  LED led_45 (.in(C_IN));
  LED led_46 (.in(C_OUT));
  LED led_47 (.in(OUT_ENABLE));
  LED led_48 (.in(ALU_OUT));
  LED led_49 (.in(SUB));
  LED led_50 (.in(JUMP));
  LED led_51 (.in(COUNTER_OUT));
  LED led_52 (.in(COUNTER_INCREMENT));
  LED led_53 (.in(RAM_A_IN));
  LED led_54 (.in(HALT));
  LED led_55 (.in(F_IN));
  LED led_56 (.in(IR_IN));
  LED led_57 (.in(IR_OUT));
  Button Reset_Computer (.out(Reset_Computer_out));
  Button Clear_Memory (.out(Clear_Memory_out));
  or or_5 (or_5_out, RAM_A_OUT, RAM_A_OUT);
  LED led_58 (.in(or_5_out));
  LED led_59 (.in(or_6_out));
  or or_6 (or_6_out, MAR_A_IN, MAR_A_IN);
  Clock clock_2 ();  // open: out
  and and_5 (Manual_Clock_2, Save_value_out, Memory_In);
  Button Save_value (.out(Save_value_out));
  // NOT_Gate not_5 is placed but not wired

  // Other names for the same wires on the sheet: Manual_Memory_In = Memory_In
endmodule

module \logic  (
  input  sc0,
  input  sc1,
  input  sc2,
  input  Bit_1,
  input  Bit_2,
  input  Bit_5,
  input  Bit_6,
  input  Flag_Register_Bit,
  input  _0_Flag,
  input  _0000,
  input  _0001,
  input  _0010,
  input  _0011,
  input  _0100,
  input  _0101,
  input  _0110,
  input  _0111,
  input  sc3,
  input  _1000,
  input  _1001,
  input  _1010,
  input  _1011,
  input  _1100,
  input  _1101,
  input  _1110,
  input  _1111,
  output COUNTER_OUT,
  output RAM_B_OUT,
  output MAR_B_IN,
  output IR_IN,
  output COUNTER_INCREMENT,
  output A_IN,
  output A_OUT,
  output B_IN,
  output B_OUT,
  output C_IN,
  output C_OUT,
  output OUT_ENABLE,
  output ALU_OUT,
  output SUB,
  output JUMP,
  output RAM_A_IN,
  output RAM_A_OUT,
  output MAR_A_IN,
  output HALT,
  output F_IN,
  output IR_OUT
);

  wire and_1_out, and_2_out, and_3_out, and_4_out, and_5_out, and_6_out, and_7_out, and_8_out, and_9_out,
       and_10_out, and_13_out, and_15_out, and_17_out, and_18_out, and_19_out, and_20_out, and_21_out,
       and_22_out, and_23_out, and_24_out, and_25_out, and_26_out, and_27_out, nor_1_out, nor_2_out,
       not_1_out, not_2_out, not_3_out, not_4_out, or_1_out, or_2_out, or_4_out, or_5_out, or_7_out;

  and and_1 (and_1_out, sc2, _0001);
  not not_1 (not_1_out, Bit_1);
  and and_2 (and_2_out, not_1_out, Bit_2);
  and and_3 (and_3_out, Bit_1, not_2_out);
  not not_2 (not_2_out, Bit_2);
  and and_4 (and_4_out, Bit_1, Bit_2);
  not not_3 (not_3_out, Bit_5);
  and and_5 (and_5_out, not_3_out, Bit_6);
  and and_6 (and_6_out, Bit_5, not_4_out);
  not not_4 (not_4_out, Bit_6);
  and and_7 (and_7_out, sc2, _0010);
  and and_8 (and_8_out, nor_1_out, and_1_out);
  nor nor_1 (nor_1_out, Bit_1, Bit_2);
  and and_9 (and_9_out, and_2_out, and_1_out);
  and and_10 (and_10_out, and_3_out, and_1_out);
  and and_11 (OUT_ENABLE, and_4_out, and_1_out);
  and and_12 (A_OUT, nor_2_out, and_1_out);
  nor nor_2 (nor_2_out, Bit_5, Bit_6);
  and and_13 (and_13_out, and_5_out, and_1_out);
  and and_14 (B_OUT, and_6_out, and_1_out);
  and and_15 (and_15_out, Bit_1, and_7_out);
  and and_16 (HALT, sc2, _0011);
  and and_17 (and_17_out, sc2, _0100);
  and and_18 (and_18_out, sc2, _0101);
  and and_19 (and_19_out, _0110, sc2);
  and and_20 (and_20_out, _0111, sc2);
  and and_21 (and_21_out, _1000, sc2);
  and and_22 (and_22_out, sc2, _1001);
  and and_23 (and_23_out, _1001, sc3);
  and and_24 (and_24_out, sc2, _1010);
  and and_25 (and_25_out, _1010, sc3);
  and and_26 (and_26_out, Flag_Register_Bit, and_18_out);
  or or_1 (or_1_out, and_26_out, and_27_out);
  and and_27 (and_27_out, _0_Flag, and_19_out);
  and and_28 (RAM_A_OUT, _0111, sc3);
  and and_29 (RAM_A_IN, _1000, sc3);
  or or_2 (or_2_out, and_17_out, or_1_out, and_20_out, and_21_out);
  or or_3 (IR_OUT, or_2_out, or_4_out);
  or or_4 (or_4_out, and_22_out, and_24_out, and_24_out, and_24_out);
  or or_5 (or_5_out, and_23_out, and_25_out);
  or or_6 (C_IN, or_5_out, or_7_out);
  or or_7 (or_7_out, and_9_out, and_7_out);
  or or_8 (B_IN, and_10_out, and_22_out, and_24_out);
  or or_9 (ALU_OUT, and_7_out, and_23_out, and_25_out);
  or or_10 (JUMP, and_17_out, or_1_out, or_1_out);
  or or_11 (F_IN, and_7_out, and_23_out, and_25_out);
  or or_12 (A_IN, and_8_out, RAM_A_OUT);
  or or_13 (C_OUT, and_13_out, RAM_A_IN);
  or or_14 (SUB, and_15_out, and_25_out);
  or or_15 (MAR_A_IN, and_20_out, and_21_out);

  assign COUNTER_INCREMENT = sc1;
  assign COUNTER_OUT = sc0;
  assign IR_IN = sc1;
  assign MAR_B_IN = sc0;
  assign RAM_B_OUT = sc1;
  // also tied to GND on the sheet: {_0000, _1011, _1100, _1101, _1110, _1111}
endmodule

module overflow (
  input  [7:0] Value_A,
  input  [7:0] Value_B,
  input  [7:0] Output_Value,
  input  SUB,
  output Overflow
);

  wire and_1_out, and_2_out, not_1_out, or_1_out, xnor_1_out;

  not not_1 (not_1_out, Value_A[7]);
  and and_1 (and_1_out, not_1_out, Value_B[7]);
  xnor xnor_1 (xnor_1_out, Value_A[7], Value_B[7]);
  and and_2 (and_2_out, xnor_1_out, Output_Value[7]);
  or or_1 (or_1_out, and_1_out, and_2_out);
  and and_3 (Overflow, or_1_out, SUB);
endmodule
